// Logisim project regsandram.circ as structural Verilog
// info.bit
module \bit  (
  input  in_1,
  input  in_2,
  output info_bit
);

  wire clock_1_out, multiplexer_1_out;

  D_Flip_Flop d_ff_1 ();  // open: clk, D, Q, Qn, preset, en, reset
  T_Flip_Flop t_ff_1 ();  // open: clk, T, Q, Qn, preset, reset, en
  Multiplexer #(.disabled(0)) multiplexer_1 (
    .in0(info_bit), .in1(in_2), .out(multiplexer_1_out), .sel(in_1));  // open: en
  Clock clock_1 (.out(clock_1_out));
  D_Flip_Flop d_ff_2 (.clk(clock_1_out), .D(multiplexer_1_out), .Q(info_bit));  // open: Qn, preset, en, reset
endmodule

module registro (
  input  in_1,
  input  [15:0] in_2,
  output [15:0] out_3
);

  \bit  bit_1 (.in_1(in_2[0]), .in_2(in_1), .info_bit(out_3[0]));
  \bit  bit_2 ();  // open: in_1, in_2, info_bit
  \bit  bit_3 ();  // open: in_1, in_2, info_bit
  \bit  bit_4 ();  // open: in_1, in_2, info_bit
  \bit  bit_5 ();  // open: in_1, in_2, info_bit
  \bit  bit_6 ();  // open: in_1, in_2, info_bit
  \bit  bit_7 ();  // open: in_1, in_2, info_bit
  \bit  bit_8 ();  // open: in_1, in_2, info_bit
  \bit  bit_9 ();  // open: in_1, in_2, info_bit
  \bit  bit_10 ();  // open: in_1, in_2, info_bit
  \bit  bit_11 ();  // open: in_1, in_2, info_bit
  \bit  bit_12 ();  // open: in_1, in_2, info_bit
  \bit  bit_13 ();  // open: in_1, in_2, info_bit
  \bit  bit_14 ();  // open: in_1, in_2, info_bit
  \bit  bit_15 ();  // open: in_1, in_2, info_bit
  \bit  bit_16 ();  // open: in_1, in_2, info_bit
endmodule

module shiftleft (
  input  in_1,
  input  [1:0] in_2,
  output [2:0] out_3
);


  assign out_3 = {in_2, in_1};
endmodule
