// Logisim project todosadders+alu+otros.circ as structural Verilog: 4 circuits, main circuit main
module main (
  input  CarryIn,
  input  [15:0] input_1__16bits,
  input  [15:0] input_2__16bits,
  output [15:0] out_4,
  output CarryOut
);

  wire fulladder_1_cout, fulladder_2_cout, fulladder_3_cout, fulladder_4_cout, fulladder_5_cout,
       fulladder_6_cout, fulladder_7_cout, fulladder_8_cout, fulladder_9_cout, fulladder_10_cout,
       fulladder_11_cout, fulladder_12_cout, fulladder_13_cout, fulladder_14_cout, fulladder_15_cout;

  fulladder fulladder_1 (
    .A(CarryIn), .B(input_1__16bits[0]), .Cin(input_2__16bits[0]), .Suma(out_4[0]), .Cout(fulladder_1_cout));
  fulladder fulladder_2 (
    .A(fulladder_1_cout), .B(input_1__16bits[1]), .Cin(input_2__16bits[1]), .Suma(out_4[1]),
    .Cout(fulladder_2_cout));
  fulladder fulladder_3 (
    .A(fulladder_2_cout), .B(input_1__16bits[2]), .Cin(input_2__16bits[2]), .Suma(out_4[2]),
    .Cout(fulladder_3_cout));
  fulladder fulladder_4 (
    .A(fulladder_3_cout), .B(input_1__16bits[3]), .Cin(input_2__16bits[3]), .Suma(out_4[3]),
    .Cout(fulladder_4_cout));
  fulladder fulladder_5 (
    .A(fulladder_4_cout), .B(input_1__16bits[4]), .Cin(input_2__16bits[4]), .Suma(out_4[4]),
    .Cout(fulladder_5_cout));
  fulladder fulladder_6 (
    .A(fulladder_5_cout), .B(input_1__16bits[5]), .Cin(input_2__16bits[5]), .Suma(out_4[5]),
    .Cout(fulladder_6_cout));
  fulladder fulladder_7 (
    .A(fulladder_6_cout), .B(input_1__16bits[6]), .Cin(input_2__16bits[6]), .Suma(out_4[6]),
    .Cout(fulladder_7_cout));
  fulladder fulladder_8 (
    .A(fulladder_7_cout), .B(input_1__16bits[7]), .Cin(input_2__16bits[7]), .Suma(out_4[7]),
    .Cout(fulladder_8_cout));
  fulladder fulladder_9 (
    .A(fulladder_8_cout), .B(input_1__16bits[8]), .Cin(input_2__16bits[8]), .Suma(out_4[8]),
    .Cout(fulladder_9_cout));
  fulladder fulladder_10 (
    .A(fulladder_9_cout), .B(input_1__16bits[9]), .Cin(input_2__16bits[9]), .Suma(out_4[9]),
    .Cout(fulladder_10_cout));
  fulladder fulladder_11 (
    .A(fulladder_10_cout), .B(input_1__16bits[10]), .Cin(input_2__16bits[10]), .Suma(out_4[10]),
    .Cout(fulladder_11_cout));
  fulladder fulladder_12 (
    .A(fulladder_11_cout), .B(input_1__16bits[11]), .Cin(input_2__16bits[11]), .Suma(out_4[11]),
    .Cout(fulladder_12_cout));
  fulladder fulladder_13 (
    .A(fulladder_12_cout), .B(input_1__16bits[12]), .Cin(input_2__16bits[12]), .Suma(out_4[12]),
    .Cout(fulladder_13_cout));
  fulladder fulladder_14 (
    .A(fulladder_13_cout), .B(input_1__16bits[13]), .Cin(input_2__16bits[13]), .Suma(out_4[13]),
    .Cout(fulladder_14_cout));
  fulladder fulladder_15 (
    .A(fulladder_14_cout), .B(input_1__16bits[14]), .Cin(input_2__16bits[14]), .Suma(out_4[14]),
    .Cout(fulladder_15_cout));
  fulladder fulladder_16 (
    .A(fulladder_15_cout), .B(input_1__16bits[15]), .Cin(input_2__16bits[15]), .Suma(out_4[15]),
    .Cout(CarryOut));
endmodule

module fulladder (
  input  A,
  input  B,
  input  Cin,
  output Suma,
  output Cout
);

  wire and_1_out, and_2_out, xor_1_out;

  xor xor_1 (xor_1_out, A, B);
  and and_1 (and_1_out, xor_1_out, Cin);
  and and_2 (and_2_out, A, B);
  xor xor_2 (Suma, xor_1_out, Cin);
  or or_1 (Cout, and_1_out, and_2_out);
endmodule

module halfadder (
  input  A,
  input  B,
  output suma,
  output Carry
);

  or or_1 (suma, A, B);
  and and_1 (Carry, A, B);
endmodule

module Inc16__1 (
  input  CarryIn,
  input  [15:0] input_1__16bits,
  input  [15:0] input_2__16bits,
  output [15:0] out_4,
  output CarryOut
);

  wire fulladder_1_cout, fulladder_2_cout, fulladder_3_cout, fulladder_4_cout, fulladder_5_cout,
       fulladder_6_cout, fulladder_7_cout, fulladder_8_cout, fulladder_9_cout, fulladder_10_cout,
       fulladder_11_cout, fulladder_12_cout, fulladder_13_cout, fulladder_14_cout, fulladder_15_cout;

  fulladder fulladder_1 (
    .A(CarryIn), .B(input_1__16bits[0]), .Cin(input_2__16bits[0]), .Suma(out_4[0]), .Cout(fulladder_1_cout));
  fulladder fulladder_2 (
    .A(fulladder_1_cout), .B(input_1__16bits[1]), .Cin(input_2__16bits[1]), .Suma(out_4[1]),
    .Cout(fulladder_2_cout));
  fulladder fulladder_3 (
    .A(fulladder_2_cout), .B(input_1__16bits[2]), .Cin(input_2__16bits[2]), .Suma(out_4[2]),
    .Cout(fulladder_3_cout));
  fulladder fulladder_4 (
    .A(fulladder_3_cout), .B(input_1__16bits[3]), .Cin(input_2__16bits[3]), .Suma(out_4[3]),
    .Cout(fulladder_4_cout));
  fulladder fulladder_5 (
    .A(fulladder_4_cout), .B(input_1__16bits[4]), .Cin(input_2__16bits[4]), .Suma(out_4[4]),
    .Cout(fulladder_5_cout));
  fulladder fulladder_6 (
    .A(fulladder_5_cout), .B(input_1__16bits[5]), .Cin(input_2__16bits[5]), .Suma(out_4[5]),
    .Cout(fulladder_6_cout));
  fulladder fulladder_7 (
    .A(fulladder_6_cout), .B(input_1__16bits[6]), .Cin(input_2__16bits[6]), .Suma(out_4[6]),
    .Cout(fulladder_7_cout));
  fulladder fulladder_8 (
    .A(fulladder_7_cout), .B(input_1__16bits[7]), .Cin(input_2__16bits[7]), .Suma(out_4[7]),
    .Cout(fulladder_8_cout));
  fulladder fulladder_9 (
    .A(fulladder_8_cout), .B(input_1__16bits[8]), .Cin(input_2__16bits[8]), .Suma(out_4[8]),
    .Cout(fulladder_9_cout));
  fulladder fulladder_10 (
    .A(fulladder_9_cout), .B(input_1__16bits[9]), .Cin(input_2__16bits[9]), .Suma(out_4[9]),
    .Cout(fulladder_10_cout));
  fulladder fulladder_11 (
    .A(fulladder_10_cout), .B(input_1__16bits[10]), .Cin(input_2__16bits[10]), .Suma(out_4[10]),
    .Cout(fulladder_11_cout));
  fulladder fulladder_12 (
    .A(fulladder_11_cout), .B(input_1__16bits[11]), .Cin(input_2__16bits[11]), .Suma(out_4[11]),
    .Cout(fulladder_12_cout));
  fulladder fulladder_13 (
    .A(fulladder_12_cout), .B(input_1__16bits[12]), .Cin(input_2__16bits[12]), .Suma(out_4[12]),
    .Cout(fulladder_13_cout));
  fulladder fulladder_14 (
    .A(fulladder_13_cout), .B(input_1__16bits[13]), .Cin(input_2__16bits[13]), .Suma(out_4[13]),
    .Cout(fulladder_14_cout));
  fulladder fulladder_15 (
    .A(fulladder_14_cout), .B(input_1__16bits[14]), .Cin(input_2__16bits[14]), .Suma(out_4[14]),
    .Cout(fulladder_15_cout));
  fulladder fulladder_16 (
    .A(fulladder_15_cout), .B(input_1__16bits[15]), .Cin(input_2__16bits[15]), .Suma(out_4[15]),
    .Cout(CarryOut));
endmodule
